// Logisim project sumador_4bites.circ as structural Verilog: 1 circuit, main circuit main
module main (
);

  wire dipswitch_2_p1, dipswitch_2_p2, dipswitch_2_p3, dipswitch_2_p4, dipswitch_3_p1, dipswitch_3_p2,
       dipswitch_3_p3, dipswitch_3_p4, dipswitch_4_sw1, dipswitch_4_sw2, dipswitch_4_sw3, n7408_1_pin1,
       n7408_1_pin2, n7408_1_pin3, n7408_1_pin4, n7408_1_pin5, n7408_1_pin6, n7408_1_pin8, n7408_1_pin11,
       n7408_1_pin12, n7408_2_pin5, n7408_3_pin1, n7408_3_pin3, n7408_3_pin5, n7408_3_pin6, n7408_3_pin8,
       n7408_3_pin9, n7408_3_pin11, n7408_4_pin11, n7408_5_pin3, n7408_5_pin11, n7408_6_pin2, n7408_7_pin1,
       n7408_7_pin3, n7408_7_pin5, n7408_7_pin11, n7408_8_pin1, n7408_8_pin3, n7408_8_pin5, n7408_8_pin11,
       n7408_9_pin11, n7408_10_pin3, n7408_10_pin6, n7408_11_pin3, n7408_11_pin6, n7408_11_pin8,
       n7408_11_pin11, n7408_12_pin8, n7408_12_pin11, n7408_13_pin3, n7432_1_pin1, n7432_1_pin2,
       n7432_1_pin3, n7432_1_pin5, n7432_1_pin6, n7432_1_pin11, n7432_1_pin12, n7432_2_pin2, n7432_2_pin3,
       n7432_2_pin6, n7432_2_pin8, n7432_2_pin11, n7432_3_pin1, n7432_3_pin2, n7432_3_pin5, n7432_3_pin6,
       n7432_3_pin8, n7432_3_pin11, n7432_3_pin12, n7432_3_pin13, n7432_4_pin1, n7432_4_pin2, n7432_4_pin3,
       n7432_4_pin5, n7432_4_pin6, n7432_4_pin8, n7432_4_pin9, n7432_4_pin11, n7432_4_pin12, n7432_4_pin13,
       n7432_5_pin3, n7432_6_pin11, n7432_9_pin11, n7486_1_pin3, n7486_1_pin5, n7486_1_pin6, n7486_1_pin7,
       n7486_1_pin14, n7486_2_pin3, n7486_2_pin5, n7486_2_pin6, n7486_2_pin8, n7486_2_pin9, n7486_2_pin11,
       n7486_3_pin8, n7486_3_pin9, n7486_3_pin11, n7486_4_pin3, n7486_4_pin7, not_1_out, not_2_out,
       not_3_out, not_6_out, not_8_out, not_9_out, not_11_out, not_13_out, not_15_out, not_18_out,
       not_19_out, not_20_out, not_21_out;

  not not_1 (not_1_out, n7408_3_pin9);
  not not_2 (not_2_out, n7408_1_pin12);
  _7408 #(.ShowInternalStructure("true")) u_7408_1 (
    .pin1(n7408_1_pin1), .pin2(n7408_1_pin2), .pin3(n7408_1_pin3), .pin4(n7408_1_pin4), .pin5(n7408_1_pin5),
    .pin6(n7408_1_pin6), .pin13(n7408_1_pin1), .pin12(n7408_1_pin12), .pin11(n7408_1_pin11),
    .pin10(not_2_out), .pin9(not_1_out), .pin8(n7408_1_pin8));
  _7432 #(.ShowInternalStructure("true")) u_7432_1 (
    .pin1(n7432_1_pin1), .pin2(n7432_1_pin2), .pin3(n7432_1_pin3), .pin4(n7432_1_pin3), .pin5(n7432_1_pin5),
    .pin6(n7432_1_pin6), .pin13(n7432_1_pin6), .pin12(n7432_1_pin12), .pin11(n7432_1_pin11));  // open: pin10, pin9, pin8
  not not_3 (not_3_out, n7408_3_pin9);
  not not_4 (n7408_1_pin5, n7408_3_pin9);
  not not_5 (n7408_1_pin2, n7408_1_pin4);
  _7_Segment_Display u_7_segment_display_1 (
    .g(n7432_5_pin3), .f(n7432_1_pin11), .e(n7432_6_pin11), .d(n7432_2_pin8));  // open: a, b, c, dp
  not not_6 (not_6_out, n7408_1_pin4);
  _7408 #(.ShowInternalStructure("true")) u_7408_2 (
    .pin1(n7408_1_pin1), .pin2(n7408_1_pin4), .pin3(n7432_1_pin12), .pin4(not_6_out), .pin5(n7408_2_pin5),
    .pin6(n7432_1_pin5), .pin13(n7408_1_pin1), .pin12(n7408_1_pin12), .pin11(n7432_1_pin2),
    .pin10(n7408_1_pin12), .pin9(not_3_out), .pin8(n7432_1_pin1));
  _7432 #(.ShowInternalStructure("true")) u_7432_2 (
    .pin1(n7408_1_pin3), .pin2(n7432_2_pin2), .pin3(n7432_2_pin3), .pin4(n7432_2_pin3), .pin5(n7408_1_pin11),
    .pin6(n7432_2_pin6), .pin13(n7408_1_pin8), .pin12(n7408_1_pin6), .pin11(n7432_2_pin11),
    .pin10(n7432_2_pin11), .pin9(n7432_2_pin6), .pin8(n7432_2_pin8));
  not not_7 (n7408_2_pin5, n7408_3_pin9);
  not not_8 (not_8_out, n7408_1_pin1);
  _7408 #(.ShowInternalStructure("true")) u_7408_3 (
    .pin1(n7408_3_pin1), .pin2(n7408_1_pin12), .pin3(n7408_3_pin3), .pin4(n7408_3_pin3), .pin5(n7408_3_pin5),
    .pin6(n7408_3_pin6), .pin13(n7408_3_pin1), .pin12(n7408_1_pin12), .pin11(n7408_3_pin11),
    .pin10(n7408_3_pin11), .pin9(n7408_3_pin9), .pin8(n7408_3_pin8));
  not not_9 (not_9_out, n7408_1_pin12);
  not not_10 (n7408_3_pin5, n7408_3_pin9);
  _7408 #(.ShowInternalStructure("true")) u_7408_4 (
    .pin13(not_8_out), .pin12(n7408_1_pin4), .pin11(n7408_4_pin11), .pin10(n7408_4_pin11), .pin9(not_9_out),
    .pin8(n7432_2_pin2));  // open: pin1, pin2, pin3, pin4, pin5, pin6
  not not_11 (not_11_out, n7408_1_pin12);
  not not_12 (n7408_3_pin1, n7408_1_pin4);
  _7432 #(.ShowInternalStructure("true")) u_7432_3 (
    .pin1(n7432_3_pin1), .pin2(n7432_3_pin2), .pin4(n7408_3_pin6), .pin5(n7432_3_pin5), .pin6(n7432_3_pin6),
    .pin13(n7432_3_pin13), .pin12(n7432_3_pin12), .pin11(n7432_3_pin11), .pin10(n7432_3_pin11),
    .pin9(n7408_3_pin8), .pin8(n7432_3_pin8));  // open: pin3
  _7408 #(.ShowInternalStructure("true")) u_7408_5 (
    .pin1(n7408_1_pin4), .pin2(n7408_1_pin12), .pin3(n7408_5_pin3), .pin4(n7408_5_pin3), .pin5(n7408_3_pin9),
    .pin6(n7432_3_pin12), .pin13(n7408_1_pin1), .pin12(n7408_1_pin4), .pin11(n7408_5_pin11),
    .pin10(n7408_5_pin11), .pin9(not_11_out), .pin8(n7432_3_pin13));
  DipSwitch #(.number(4)) dipswitch_1 (.sw1(n7408_1_pin1), .sw2(n7408_1_pin4), .sw3(n7408_1_pin12), .sw4(n7408_3_pin9));
  not not_13 (not_13_out, n7408_3_pin9);
  _7432 #(.ShowInternalStructure("true")) u_7432_4 (
    .pin1(n7432_4_pin1), .pin2(n7432_4_pin2), .pin3(n7432_4_pin3), .pin4(n7432_4_pin3), .pin5(n7432_4_pin5),
    .pin6(n7432_4_pin6), .pin13(n7432_4_pin13), .pin12(n7432_4_pin12), .pin11(n7432_4_pin11),
    .pin10(n7432_4_pin11), .pin9(n7432_4_pin9), .pin8(n7432_4_pin8));
  _7408 #(.ShowInternalStructure("true")) u_7408_6 (
    .pin1(n7408_1_pin1), .pin2(n7408_6_pin2), .pin3(n7432_4_pin2), .pin4(n7408_6_pin2), .pin5(n7408_1_pin12),
    .pin6(n7432_4_pin1), .pin13(n7408_1_pin1), .pin12(n7408_3_pin9), .pin11(n7432_4_pin13),
    .pin10(not_13_out), .pin9(n7408_1_pin12), .pin8(n7432_4_pin12));
  _7432 #(.ShowInternalStructure("true")) u_7432_5 (
    .pin1(n7432_3_pin6), .pin2(n7432_3_pin8), .pin3(n7432_5_pin3));  // open: pin4, pin5, pin6, pin13, pin12, pin11, pin10, pin9, pin8
  not not_14 (n7408_6_pin2, n7408_1_pin4);
  not not_15 (not_15_out, n7408_1_pin12);
  _7408 #(.ShowInternalStructure("true")) u_7408_7 (
    .pin1(n7408_7_pin1), .pin2(n7408_1_pin12), .pin3(n7408_7_pin3), .pin4(n7408_7_pin3), .pin5(n7408_7_pin5),
    .pin6(n7432_3_pin2), .pin13(n7408_1_pin4), .pin12(not_15_out), .pin11(n7408_7_pin11),
    .pin10(n7408_7_pin11), .pin9(n7408_3_pin9), .pin8(n7432_3_pin1));
  not not_16 (n7408_7_pin1, n7408_1_pin1);
  _7432 #(.ShowInternalStructure("true")) u_7432_6 (
    .pin13(n7432_4_pin6), .pin12(n7432_4_pin8), .pin11(n7432_6_pin11));  // open: pin1, pin2, pin3, pin4, pin5, pin6, pin10, pin9, pin8
  // DipSwitch #(.number(4)) dipswitch_2: pin names not known; wires that end beside it: dipswitch_2_p1, dipswitch_2_p2, dipswitch_2_p3, dipswitch_2_p4
  // DipSwitch #(.number(4)) dipswitch_3: pin names not known; wires that end beside it: dipswitch_3_p1, dipswitch_3_p2, dipswitch_3_p3, dipswitch_3_p4
  not not_17 (n7408_7_pin5, n7408_3_pin9);
  not not_18 (not_18_out, n7408_1_pin12);
  not not_19 (not_19_out, n7408_3_pin9);
  not not_20 (not_20_out, n7408_1_pin12);
  not not_21 (not_21_out, n7408_1_pin4);
  _7408 #(.ShowInternalStructure("true")) u_7408_8 (
    .pin1(n7408_8_pin1), .pin2(n7408_1_pin4), .pin3(n7408_8_pin3), .pin4(n7408_8_pin3), .pin5(n7408_8_pin5),
    .pin6(n7432_4_pin9), .pin13(n7408_1_pin4), .pin12(not_18_out), .pin11(n7408_8_pin11),
    .pin10(n7408_8_pin11), .pin9(n7408_3_pin9), .pin8(n7432_4_pin5));
  not not_22 (n7408_8_pin1, n7408_1_pin1);
  not not_23 (n7408_8_pin5, n7408_3_pin9);
  _7408 #(.ShowInternalStructure("true")) u_7408_9 (
    .pin13(not_21_out), .pin12(not_20_out), .pin11(n7408_9_pin11), .pin10(n7408_9_pin11), .pin9(not_19_out),
    .pin8(n7432_3_pin5));  // open: pin1, pin2, pin3, pin4, pin5, pin6
  _7486 #(.ShowInternalStructure("true"), .VccGndPorts("true")) u_7486_1 (
    .pin1(dipswitch_2_p1), .pin2(dipswitch_3_p1), .pin3(n7486_1_pin3), .pin4(n7486_1_pin3),
    .pin5(n7486_1_pin5), .pin6(n7486_1_pin6), .pin7(n7486_1_pin7), .pin14(n7486_1_pin14));  // open: pin13, pin12, pin11, pin10, pin9, pin8
  _7486 #(.ShowInternalStructure("true"), .VccGndPorts("true")) u_7486_2 (
    .pin1(dipswitch_2_p3), .pin2(dipswitch_3_p3), .pin3(n7486_2_pin3), .pin4(n7486_2_pin3),
    .pin5(n7486_2_pin5), .pin6(n7486_2_pin6), .pin7(n7486_1_pin7), .pin14(n7486_1_pin14),
    .pin13(dipswitch_2_p2), .pin12(dipswitch_3_p2), .pin11(n7486_2_pin11), .pin10(n7486_2_pin11),
    .pin9(n7486_2_pin9), .pin8(n7486_2_pin8));
  _7486 #(.ShowInternalStructure("true"), .VccGndPorts("true")) u_7486_3 (
    .pin7(n7486_1_pin7), .pin14(n7486_1_pin14), .pin13(dipswitch_2_p4), .pin12(dipswitch_3_p4),
    .pin11(n7486_3_pin11), .pin10(n7486_3_pin11), .pin9(n7486_3_pin9), .pin8(n7486_3_pin8));  // open: pin1, pin2, pin3, pin4, pin5, pin6
  DipSwitch #(.number(3)) dipswitch_4 (.sw1(dipswitch_4_sw1), .sw2(dipswitch_4_sw2), .sw3(dipswitch_4_sw3));
  _7486 #(.VccGndPorts("true")) u_7486_4 (
    .pin1(dipswitch_4_sw1), .pin2(dipswitch_4_sw2), .pin3(n7486_4_pin3), .pin7(n7486_4_pin7),
    .pin14(dipswitch_4_sw3));  // open: pin4, pin5, pin6, pin13, pin12, pin11, pin10, pin9, pin8
  _7408 #(.ShowInternalStructure("true"), .VccGndPorts("true")) u_7408_10 (
    .pin1(dipswitch_2_p1), .pin2(dipswitch_3_p1), .pin3(n7408_10_pin3), .pin4(n7486_1_pin3),
    .pin5(n7486_1_pin5), .pin6(n7408_10_pin6), .pin7(n7486_1_pin7), .pin14(n7486_1_pin14));  // open: pin13, pin12, pin11, pin10, pin9, pin8
  _7408 #(.ShowInternalStructure("true"), .VccGndPorts("true")) u_7408_11 (
    .pin1(dipswitch_2_p3), .pin2(dipswitch_3_p3), .pin3(n7408_11_pin3), .pin4(n7486_2_pin3),
    .pin5(n7486_2_pin5), .pin6(n7408_11_pin6), .pin7(n7486_1_pin7), .pin14(n7486_1_pin14),
    .pin13(dipswitch_3_p2), .pin12(dipswitch_2_p2), .pin11(n7408_11_pin11), .pin10(n7486_2_pin11),
    .pin9(n7486_2_pin9), .pin8(n7408_11_pin8));
  _7408 #(.ShowInternalStructure("true"), .VccGndPorts("true")) u_7408_12 (
    .pin7(n7486_1_pin7), .pin14(n7486_1_pin14), .pin13(dipswitch_2_p4), .pin12(dipswitch_3_p4),
    .pin11(n7408_12_pin11), .pin10(n7486_3_pin11), .pin9(n7486_3_pin9), .pin8(n7408_12_pin8));  // open: pin1, pin2, pin3, pin4, pin5, pin6
  _7408 #(.VccGndPorts("true")) u_7408_13 (
    .pin1(dipswitch_4_sw1), .pin2(dipswitch_4_sw2), .pin3(n7408_13_pin3), .pin7(n7486_4_pin7),
    .pin14(dipswitch_4_sw3));  // open: pin4, pin5, pin6, pin13, pin12, pin11, pin10, pin9, pin8
  _7432 #(.ShowInternalStructure("true"), .VccGndPorts("true")) u_7432_7 (
    .pin1(n7408_10_pin3), .pin2(n7408_10_pin6), .pin3(n7486_2_pin9), .pin7(n7486_1_pin7),
    .pin14(n7486_1_pin14));  // open: pin4, pin5, pin6, pin13, pin12, pin11, pin10, pin9, pin8
  _7432 #(.ShowInternalStructure("true"), .VccGndPorts("true")) u_7432_8 (
    .pin1(n7408_11_pin3), .pin2(n7408_11_pin6), .pin3(n7486_3_pin9), .pin7(n7486_1_pin7),
    .pin14(n7486_1_pin14), .pin13(n7408_11_pin11), .pin12(n7408_11_pin8), .pin11(n7486_2_pin5));  // open: pin4, pin5, pin6, pin10, pin9, pin8
  _7432 #(.ShowInternalStructure("true"), .VccGndPorts("true")) u_7432_9 (
    .pin7(n7486_1_pin7), .pin14(n7486_1_pin14), .pin13(n7408_12_pin11), .pin12(n7408_12_pin8),
    .pin11(n7432_9_pin11));  // open: pin1, pin2, pin3, pin4, pin5, pin6, pin10, pin9, pin8
  LED led_1 (.in(n7486_4_pin3));
  LED led_2 (.in(n7408_13_pin3));
  LedBar #(.matrixcols(4)) Suma (.led0(n7486_3_pin8), .led1(n7486_2_pin6), .led2(n7486_2_pin8), .led3(n7486_1_pin6));
  LED Carreo (.in(n7432_9_pin11));
  // also tied to GND on the sheet: {n7486_1_pin5, n7486_4_pin7, n7486_1_pin7}
  // also tied to VCC on the sheet: n7486_1_pin14

  // Notes on the sheet:
  //   1 bit
  //   2 bit
  //   3 bit
  //   4 bit
  //   <<<
endmodule
