// Logisim project sumador_inversor.circ as structural Verilog
module main (
  input  [7:0] in_1,
  input  in_2,
  input  [7:0] in_3,
  output [7:0] out_4
);

  wire button_1_out, n74283_1_pin9, n74283_2_pin9;
  wire [7:0] n74283_1_pin4;

  _74283 #(.ShowInternalStructure("true")) u_74283_1 (
    .pin1(n74283_1_pin4[1]), .pin2(in_3[1]), .pin3(in_1[1]), .pin4(n74283_1_pin4[0]), .pin5(in_1[0]),
    .pin6(in_3[0]), .pin7(in_2), .pin15(in_3[2]), .pin14(in_1[2]), .pin13(n74283_1_pin4[2]), .pin12(in_1[3]),
    .pin11(in_3[3]), .pin10(n74283_1_pin4[3]), .pin9(n74283_1_pin9));
  _74283 #(.ShowInternalStructure("true")) u_74283_2 (
    .pin1(n74283_1_pin4[5]), .pin2(in_3[5]), .pin3(in_1[5]), .pin4(n74283_1_pin4[4]), .pin5(in_1[4]),
    .pin6(in_3[4]), .pin7(n74283_1_pin9), .pin15(in_3[6]), .pin14(in_1[6]), .pin13(n74283_1_pin4[6]),
    .pin12(in_1[7]), .pin11(in_3[7]), .pin10(n74283_1_pin4[7]), .pin9(n74283_2_pin9));
  LED led_1 (.in(n74283_2_pin9));
  LED led_2 (.in(n74283_1_pin9));
  LedBar ledbar_1 (
    .led0(n74283_1_pin4[7]), .led1(n74283_1_pin4[6]), .led2(n74283_1_pin4[5]), .led3(n74283_1_pin4[4]),
    .led4(n74283_1_pin4[3]), .led5(n74283_1_pin4[2]), .led6(n74283_1_pin4[1]), .led7(n74283_1_pin4[0]));
  Button button_1 (.out(button_1_out));
  inversor inversor_1 (.in_1(n74283_1_pin4), .in_2(button_1_out), .out_3(out_4));
endmodule

module inversor (
  input  [7:0] in_1,
  input  in_2,
  output [7:0] out_3
);

  wire [7:0] n7414_1_pin12;

  _7414 #(.ShowInternalStructure("true")) u_7414_1 (
    .pin1(in_1[3]), .pin2(n7414_1_pin12[3]), .pin3(in_1[4]), .pin4(n7414_1_pin12[4]), .pin5(in_1[5]),
    .pin6(n7414_1_pin12[5]), .pin13(in_1[0]), .pin12(n7414_1_pin12[0]), .pin11(in_1[1]),
    .pin10(n7414_1_pin12[1]), .pin9(in_1[2]), .pin8(n7414_1_pin12[2]));
  _7414 #(.ShowInternalStructure("true")) u_7414_2 (
    .pin13(in_1[6]), .pin12(n7414_1_pin12[6]), .pin11(in_1[7]), .pin10(n7414_1_pin12[7]));  // open: pin1, pin2, pin3, pin4, pin5, pin6, pin9, pin8
  Multiplexer #(.width(8)) multiplexer_1 (.in0(in_1), .in1(n7414_1_pin12), .out(out_3), .sel(in_2));
endmodule
