// Logisim project sumador_inversor7.0.circ as structural Verilog: 14 circuits, main circuit main
module main (
  input  Pin_BUS2,
  input  Pin_BUS1,
  input  PIN_BUS3,
  input  [7:0] ENTRADA,
  input  PIN_registro1,
  input  reset1,
  input  PIN_registro2,
  input  [2:0] OP,
  input  Reset2,
  input  PIN_BUS4,
  output [7:0] SALIDA
);

  wire alu_1_carreo_resta, alu_1_carreo_suma, BUS_1REGISTRO_pin1, BUS_2REGISTRO_pin1, BUS_ENTRADA_pin1,
       BUS_SALIDA_pin1, not_1_out, not_2_out, not_3_out, not_4_out;
  wire [7:0] BUS_SALIDA_pin9, register_1_q, register_2_q;

  not not_1 (not_1_out, Pin_BUS1);
  _74245 #(.ShowInternalStructure("true")) BUS_ENTRADA (
    .pin1(BUS_ENTRADA_pin1), .pin2(ENTRADA[7]), .pin3(ENTRADA[6]), .pin4(ENTRADA[5]), .pin5(ENTRADA[4]),
    .pin6(ENTRADA[3]), .pin7(ENTRADA[2]), .pin8(ENTRADA[1]), .pin9(ENTRADA[0]), .pin19(not_1_out),
    .pin18(SALIDA[7]), .pin17(SALIDA[6]), .pin16(SALIDA[5]), .pin15(SALIDA[4]), .pin14(SALIDA[3]),
    .pin13(SALIDA[2]), .pin12(SALIDA[1]), .pin11(SALIDA[0]));
  Register register_1 (.D(SALIDA), .en(PIN_registro1), .clk(PIN_registro1), .Q(register_1_q), .clr(reset1));
  Register register_2 (.D(SALIDA), .en(PIN_registro2), .clk(PIN_registro2), .Q(register_2_q), .clr(Reset2));
  Hex_Digit_Display hex_digit_display_1 (.value(SALIDA[7:4]));  // open: dp
  Hex_Digit_Display hex_digit_display_2 (.value(SALIDA[3:0]));  // open: dp
  not not_2 (not_2_out, Pin_BUS2);
  _74245 #(.ShowInternalStructure("true")) BUS_1REGISTRO (
    .pin1(BUS_1REGISTRO_pin1), .pin2(register_1_q[7]), .pin3(register_1_q[6]), .pin4(register_1_q[5]),
    .pin5(register_1_q[4]), .pin6(register_1_q[3]), .pin7(register_1_q[2]), .pin8(register_1_q[1]),
    .pin9(register_1_q[0]), .pin19(not_2_out), .pin18(SALIDA[7]), .pin17(SALIDA[6]), .pin16(SALIDA[5]),
    .pin15(SALIDA[4]), .pin14(SALIDA[3]), .pin13(SALIDA[2]), .pin12(SALIDA[1]), .pin11(SALIDA[0]));
  LedBar ledbar_1 (
    .led0(register_1_q[7]), .led1(register_1_q[6]), .led2(register_1_q[5]), .led3(register_1_q[4]),
    .led4(register_1_q[3]), .led5(register_1_q[2]), .led6(register_1_q[1]), .led7(register_1_q[0]));
  not not_3 (not_3_out, PIN_BUS4);
  _74245 #(.ShowInternalStructure("true")) BUS_2REGISTRO (
    .pin1(BUS_2REGISTRO_pin1), .pin2(register_2_q[7]), .pin3(register_2_q[6]), .pin4(register_2_q[5]),
    .pin5(register_2_q[4]), .pin6(register_2_q[3]), .pin7(register_2_q[2]), .pin8(register_2_q[1]),
    .pin9(register_2_q[0]), .pin19(not_3_out), .pin18(SALIDA[7]), .pin17(SALIDA[6]), .pin16(SALIDA[5]),
    .pin15(SALIDA[4]), .pin14(SALIDA[3]), .pin13(SALIDA[2]), .pin12(SALIDA[1]), .pin11(SALIDA[0]));
  LedBar ledbar_2 (
    .led0(register_2_q[7]), .led1(register_2_q[6]), .led2(register_2_q[5]), .led3(register_2_q[4]),
    .led4(register_2_q[3]), .led5(register_2_q[2]), .led6(register_2_q[1]), .led7(register_2_q[0]));
  not not_4 (not_4_out, PIN_BUS3);
  _74245 #(.ShowInternalStructure("true")) BUS_SALIDA (
    .pin1(BUS_SALIDA_pin1), .pin2(BUS_SALIDA_pin9[7]), .pin3(BUS_SALIDA_pin9[6]), .pin4(BUS_SALIDA_pin9[5]),
    .pin5(BUS_SALIDA_pin9[4]), .pin6(BUS_SALIDA_pin9[3]), .pin7(BUS_SALIDA_pin9[2]),
    .pin8(BUS_SALIDA_pin9[1]), .pin9(BUS_SALIDA_pin9[0]), .pin19(not_4_out), .pin18(SALIDA[7]),
    .pin17(SALIDA[6]), .pin16(SALIDA[5]), .pin15(SALIDA[4]), .pin14(SALIDA[3]), .pin13(SALIDA[2]),
    .pin12(SALIDA[1]), .pin11(SALIDA[0]));
  LedBar ledbar_3 (
    .led0(BUS_SALIDA_pin9[7]), .led1(BUS_SALIDA_pin9[6]), .led2(BUS_SALIDA_pin9[5]),
    .led3(BUS_SALIDA_pin9[4]), .led4(BUS_SALIDA_pin9[3]), .led5(BUS_SALIDA_pin9[2]),
    .led6(BUS_SALIDA_pin9[1]), .led7(BUS_SALIDA_pin9[0]));
  ALU alu_1 (
    .EntradaA(register_1_q), .EntradaB(register_2_q), .OP(OP), .Carreo_Suma(alu_1_carreo_suma),
    .Salida(BUS_SALIDA_pin9), .Carreo_Resta(alu_1_carreo_resta));
  LED led_1 (.in(alu_1_carreo_suma));
  LED led_2 (.in(alu_1_carreo_resta));
  // also tied to VCC on the sheet: {BUS_ENTRADA_pin1, BUS_1REGISTRO_pin1, BUS_2REGISTRO_pin1, BUS_SALIDA_pin1}
endmodule

module inversor (
  input  [7:0] ent,
  input  bot,
  output [7:0] inv
);

  wire [7:0] n7414_1_pin12;

  _7414 #(.ShowInternalStructure("true")) u_7414_1 (
    .pin1(ent[3]), .pin2(n7414_1_pin12[3]), .pin3(ent[4]), .pin4(n7414_1_pin12[4]), .pin5(ent[5]),
    .pin6(n7414_1_pin12[5]), .pin13(ent[0]), .pin12(n7414_1_pin12[0]), .pin11(ent[1]),
    .pin10(n7414_1_pin12[1]), .pin9(ent[2]), .pin8(n7414_1_pin12[2]));
  _7414 #(.ShowInternalStructure("true")) u_7414_2 (
    .pin13(ent[6]), .pin12(n7414_1_pin12[6]), .pin11(ent[7]), .pin10(n7414_1_pin12[7]));  // open: pin1, pin2, pin3, pin4, pin5, pin6, pin9, pin8
  Multiplexer #(.width(8)) multiplexer_1 (.in0(ent), .in1(n7414_1_pin12), .out(inv), .sel(bot));
endmodule

module ALU (
  input  [7:0] EntradaA,
  input  [7:0] EntradaB,
  input  [2:0] OP,
  output Carreo_Suma,
  output [7:0] Salida,
  output Carreo_Resta
);

  wire [7:0] desplazador_1_out_3, desplazador_dere_1_out_3, o_1_out_3, resta_1_salida, suma_1_salida,
       xo_1_out_3, y_1_out_3;

  Suma suma_1 (.Entrada1(EntradaA), .Entrada2(EntradaB), .Salida(suma_1_salida), .Acarreo(Carreo_Suma));
  Resta resta_1 (.Entrada1(EntradaA), .Entrada2(EntradaB), .Salida(resta_1_salida), .Acarreo(Carreo_Resta));
  Y y_1 (.in_1(EntradaA), .in_2(EntradaB), .out_3(y_1_out_3));
  O o_1 (.in_1(EntradaA), .in_2(EntradaB), .out_3(o_1_out_3));
  xo xo_1 (.in_1(EntradaA), .in_2(EntradaB), .out_3(xo_1_out_3));
  Desplazador desplazador_1 (.in_1(EntradaA), .in_2(EntradaB[2:0]), .out_3(desplazador_1_out_3));
  Desplazador_dere desplazador_dere_1 (.in_1(EntradaB), .in_2(EntradaB[2:0]), .out_3(desplazador_dere_1_out_3));
  Multiplexer #(.select(3), .width(8)) multiplexer_1 (
    .in0(suma_1_salida), .in1(resta_1_salida), .in2(y_1_out_3), .in3(o_1_out_3), .in4(xo_1_out_3),
    .in5(desplazador_1_out_3), .in6(desplazador_dere_1_out_3), .out(Salida), .sel(OP));  // open: in7
endmodule

module Suma (
  input  [7:0] Entrada1,
  input  [7:0] Entrada2,
  output [7:0] Salida,
  output Acarreo
);

  wire n74283_1_pin7, n74283_1_pin9;

  _74283 #(.ShowInternalStructure("true")) u_74283_1 (
    .pin1(Salida[1]), .pin2(Entrada2[1]), .pin3(Entrada1[1]), .pin4(Salida[0]), .pin5(Entrada1[0]),
    .pin6(Entrada2[0]), .pin7(n74283_1_pin7), .pin15(Entrada2[2]), .pin14(Entrada1[2]), .pin13(Salida[2]),
    .pin12(Entrada1[3]), .pin11(Entrada2[3]), .pin10(Salida[3]), .pin9(n74283_1_pin9));
  _74283 #(.ShowInternalStructure("true")) u_74283_2 (
    .pin1(Salida[5]), .pin2(Entrada2[5]), .pin3(Entrada1[5]), .pin4(Salida[4]), .pin5(Entrada1[4]),
    .pin6(Entrada2[4]), .pin7(n74283_1_pin9), .pin15(Entrada2[6]), .pin14(Entrada1[6]), .pin13(Salida[6]),
    .pin12(Entrada1[7]), .pin11(Entrada2[7]), .pin10(Salida[7]), .pin9(Acarreo));
  LED led_1 (.in(n74283_1_pin9));
  // also tied to GND on the sheet: n74283_1_pin7
endmodule

module Resta (
  input  [7:0] Entrada1,
  input  [7:0] Entrada2,
  output [7:0] Salida,
  output Acarreo
);

  wire n74283_1_pin7, n74283_1_pin9, n74283_3_pin3;
  wire [0:0] inversor_1_inv;
  wire [7:0] n74283_1_pin6;

  _74283 #(.ShowInternalStructure("true")) u_74283_1 (
    .pin1(Salida[1]), .pin2(n74283_1_pin6[1]), .pin3(Entrada1[1]), .pin4(Salida[0]), .pin5(Entrada1[0]),
    .pin6(n74283_1_pin6[0]), .pin7(n74283_1_pin7), .pin15(n74283_1_pin6[2]), .pin14(Entrada1[2]),
    .pin13(Salida[2]), .pin12(Entrada1[3]), .pin11(n74283_1_pin6[3]), .pin10(Salida[3]), .pin9(n74283_1_pin9));
  _74283 #(.ShowInternalStructure("true")) u_74283_2 (
    .pin1(Salida[5]), .pin2(n74283_1_pin6[5]), .pin3(Entrada1[5]), .pin4(Salida[4]), .pin5(Entrada1[4]),
    .pin6(n74283_1_pin6[4]), .pin7(n74283_1_pin9), .pin15(n74283_1_pin6[6]), .pin14(Entrada1[6]),
    .pin13(Salida[6]), .pin12(Entrada1[7]), .pin11(n74283_1_pin6[7]), .pin10(Salida[7]), .pin9(Acarreo));
  inversor inversor_1 (.ent(Entrada2), .bot(1'b1), .inv({n74283_1_pin6[7:1], inversor_1_inv[0]}));
  _74283 #(.ShowInternalStructure("true")) u_74283_3 (
    .pin1(n74283_1_pin6[0]), .pin2(inversor_1_inv[0]), .pin3(n74283_3_pin3));  // open: pin4, pin5, pin6, pin7, pin15, pin14, pin13, pin12, pin11, pin10, pin9
  LED led_1 (.in(n74283_1_pin9));
  // also tied to GND on the sheet: n74283_1_pin7
  // also tied to VCC on the sheet: n74283_3_pin3
endmodule

module Y (
  input  [7:0] in_1,
  input  [7:0] in_2,
  output [7:0] out_3
);

  assign out_3 = in_1 & in_2;  // AND_Gate and_1, 8 bits wide
endmodule

module Desplazador (
  input  [7:0] in_1,
  input  [2:0] in_2,
  output [7:0] out_3
);

  Shifter shifter_1 (.in(in_1), .\dist (in_2), .out(out_3));
endmodule

module O (
  input  [7:0] in_1,
  input  [7:0] in_2,
  output [7:0] out_3
);

  assign out_3 = in_1 | in_2;  // OR_Gate or_1, 8 bits wide
endmodule

module xo (
  input  [7:0] in_1,
  input  [7:0] in_2,
  output [7:0] out_3
);

  assign out_3 = in_1 ^ in_2;  // XOR_Gate xor_1, 8 bits wide
endmodule

module Desplazador_dere (
  input  [7:0] in_1,
  input  [2:0] in_2,
  output [7:0] out_3
);

  Shifter #(.shift("lr")) shifter_1 (.in(in_1), .\dist (in_2), .out(out_3));
endmodule

module compu (
  input  in_1,
  input  in_2,
  input  [7:0] in_3,
  input  in_4,
  input  in_5,
  input  [7:0] in_6,
  output [7:0] out_7,
  output [7:0] out_8
);

  wire clock_1_out;
  wire [7:0] counter_1_q;
  wire [18:0] rom_1_data;

  Counter counter_1 (.clr(in_1), .clk(in_2), .Q(counter_1_q));  // open: load, up, count, D, carry
  ROM #(.dataWidth(19)) rom_1 (.addr(counter_1_q), .data(rom_1_data));
  ROM rom_2 ();  // open: addr, data
  Clock clock_1 (.out(clock_1_out));
  RAM ram_1 (.addr(in_3), .we(in_4), .oe(in_5), .clk(clock_1_out), .din(in_6), .dout(out_8));
  main ALU (
    .Pin_BUS1(rom_1_data[18]), .ENTRADA(rom_1_data[7:0]), .reset1(rom_1_data[9]), .Reset2(rom_1_data[8]),
    .PIN_registro1(rom_1_data[14]), .PIN_registro2(rom_1_data[13]), .Pin_BUS2(rom_1_data[17]),
    .PIN_BUS4(rom_1_data[15]), .OP(rom_1_data[12:10]), .PIN_BUS3(rom_1_data[16]), .SALIDA(out_7));

  // Notes on the sheet:
  //   contents of rom_1 (hex, n*v repeats v):
  //   40005 44005 5 40007 42007 7 10000 14000 0 40003 42003 3 400 10400 14400 400 40001 42001 1 1400 11400
endmodule

module Compu_ram (
  input  Reset_Contador,
  input  Boton_manual,
  input  Boton_automatco,
  input  [7:0] Entrada,
  output [7:0] Salida
);

  wire reloj_auto_manual_1_out_5, undriven_2;
  wire [7:0] counter_1_q, ram_2_dout, undriven, undriven_3;
  wire [20:0] rom_1_data;

  Reloj_auto_manual reloj_auto_manual_1 (
    .MANUAL(Boton_manual), .AUTO(Boton_automatco), .ENTRAD(Entrada), .out_5(reloj_auto_manual_1_out_5));  // open: in_4
  Counter counter_1 (
    .clr(Reset_Contador), .clk(reloj_auto_manual_1_out_5), .Q(counter_1_q));  // open: load, up, count, D, carry
  ROM #(.dataWidth(21)) rom_1 (.addr(counter_1_q), .data(rom_1_data));
  RAM ram_1 (.addr(undriven_3), .we(undriven_2), .din(undriven));  // open: oe, clk, dout
  RAM ram_2 (
    .addr(rom_1_data[9:2]), .we(rom_1_data[1]), .oe(rom_1_data[0]), .clk(reloj_auto_manual_1_out_5),
    .din(Entrada), .dout(ram_2_dout));
  main ALU (
    .Pin_BUS1(rom_1_data[20]), .ENTRADA(ram_2_dout), .reset1(rom_1_data[11]), .Reset2(rom_1_data[10]),
    .PIN_registro1(rom_1_data[16]), .PIN_registro2(rom_1_data[15]), .Pin_BUS2(rom_1_data[19]),
    .PIN_BUS4(rom_1_data[17]), .OP(rom_1_data[14:12]), .PIN_BUS3(rom_1_data[18]), .SALIDA(Salida));

  // Notes on the sheet:
  //   contents of rom_1 (hex, n*v repeats v):
  //   2 6 a e 1 100001 110001 1 5 100005 108005 5 40000 50000 0 9 100009 108009 9 1000 41000 51000 1000 d
  //   10000d 10800d d 5000 45000
endmodule

module Final (
  input  in_1,
  input  [7:0] in_2,
  output [7:0] out_3
);

  wire button_1_out, button_2_out;

  Button button_1 (.out(button_1_out));
  Button button_2 (.out(button_2_out));
  Compu_ram compu_ram_1 (
    .Reset_Contador(button_1_out), .Boton_manual(button_2_out), .Boton_automatco(in_1), .Entrada(in_2),
    .Salida(out_3));
endmodule

module Reloj_auto_manual (
  input  MANUAL,
  input  AUTO,
  input  [7:0] ENTRAD,
  input  [7:0] in_4,
  output out_5
);

  wire clock_1_out, comparator_1_eq, not_1_out, t_ff_1_q;

  Comparator comparator_1 (.a(ENTRAD), .b(in_4), .eq(comparator_1_eq));  // open: gt, lt
  not not_1 (not_1_out, comparator_1_eq);
  Clock clock_1 (.out(clock_1_out));
  T_Flip_Flop t_ff_1 (.T(not_1_out), .clk(clock_1_out), .Q(t_ff_1_q));  // open: Qn, reset, preset
  Multiplexer multiplexer_1 (.in0(MANUAL), .in1(t_ff_1_q), .out(out_5), .sel(AUTO));
endmodule
